# Fritzing sketch beehive monitor3 (saved by Fritzing 0.9.3b)
circuit board: 8.46667cm x 5.64444cm
breadboards: 1

parts:
  Onderdeel1 = Logic Level Converter
  DHT1 = DHT22 Humidity and Temperature Sensor
  DS1 = DS18B20 1-Wire Temperature Sensor Probe Cable
  DS2 = DS18B20 1-Wire Temperature Sensor Probe Cable
  S1 = Toggle Switch [package=THT]
  Onderdeel2 = Arduino MKR1000
  R1 = Resistor [tolerance=±5% resistance=4.7k package=THT]
  J1 = female pin header, 6 pins [form="♀ (female)"]
  J2 = female pin header, 4 pins [form="♀ (female)"]
  R2 = Resistor [tolerance=±5% resistance=4.7k package=THT]

nets:
  GND: Onderdeel1.GND, S1.COM, Onderdeel2.GND, J1.pin4
  N1: Onderdeel1.LV, Onderdeel2.VIN
  N2: Onderdeel1.RX_LV, Onderdeel2.D11_SDA
  N3: Onderdeel1.TX_LV, Onderdeel2.D12_SCL
  N4: Onderdeel1.TX_HV, J1.pin1
  N5: Onderdeel1.RX_HV, J1.pin2
  N6: Onderdeel1.HV, J1.pin3
  N7: Onderdeel1.RX2_HV, J1.pin5
  N8: Onderdeel1.TX2_HV, J1.pin6
  VDD: DHT1.VDD, DS1.VDD, DS1.shield, DS2.VDD, DS2.shield, Onderdeel2.D3_PWM, R1.Pin_0, R1.Pin_1, J2.pin1, J2.pin2, R2.Pin_1
  N9: DHT1.DATA, Onderdeel2.D2_PWM, R2.Pin_0
  GND_2: DHT1.GND, DS1.GND, DS2.GND
  N10: DS1.DQ, DS2.DQ
  N11: S1.L2, Onderdeel2.D7
  N12: Onderdeel2.D4_PWM, J2.pin3
  N13: Onderdeel2.D5_PWM, J2.pin4

custom parts:
  Arduino MKR1000: MKR1000 is a powerful board that combines the functionality of the Zero and the Wi-Fi Shield. It is the ideal solution for makers wanting to design IoT projects with minimal previous experience in networking
